// Logisim project InputHandler.circ as structural Verilog: 2 circuits, main circuit ExpDiff12
// ExpDiff
module ExpDiff12 (
  input  SA,
  input  SB,
  input  [10:0] A,
  input  [10:0] B,
  output Switch,
  output A_B,
  output [11:0] A_nB,
  output [11:0] Exp_Large
);

  wire [10:0] n12mux2x1_1_o;

  _11BitMagnitudeComparator u_11bitmagnitudecomparator_1 (.SA(SA), .SB(SB), .A(A), .B(B), .Switch(Switch), .A_B(A_B));
  _12Mux2X1 u_12mux2x1_1 (.A(A), .B(B), .E_prime(1'b0), .S(A_B), .O(n12mux2x1_1_o));
  // _12Mux2X1 12mux2x1_2: pin names not known; wires that end beside it: B, A, 1'b0, A_B, Exp_Large
endmodule

// InpProc
module InputHandle (
  input  SA,
  input  SB,
  input  [31:0] A_Frac,
  input  [31:0] B_Frac,
  input  [11:0] A_Exp,
  input  [11:0] B_Exp,
  output Switch,
  output [31:0] Large,
  output [31:0] Small,
  output [11:0] ExpDiff,
  output [11:0] Exp_Large,
  output A_B
);

  // ExpDiff12 expdiff12_1: pin names not known; wires that end beside it: SA, SB, A_Exp, B_Exp, Switch, A_B, ExpDiff, Exp_Large
  _32Mux2X1 u_32mux2x1_1 (.A(B_Frac), .B(A_Frac), .E_prime(1'b0), .S(A_B), .O(Large));
  _32Mux2X1 u_32mux2x1_2 (.A(A_Frac), .B(B_Frac), .E_prime(1'b0), .S(A_B), .O(Small));
endmodule
